// Logisim project control_logic.circ as structural Verilog: 1 circuit, main circuit control_logic
module control_logic (
  input  [31:0] inst,
  input  BrEq,
  input  BrLt,
  output PCSel,
  output RegWEn,
  output [2:0] ImmSel,
  output BrUn,
  output ASel,
  output BSel,
  output [3:0] ALUSel,
  output MemRW,
  output [1:0] WBSel
);

  wire add0ins, addiins, and1ins, and_3_out, and_4_out, and_8_out, and_21_out, and_22_out, and_23_out,
       and_25_out, and_26_out, and_27_out, and_28_out, and_35_out, and_36_out, and_37_out, and_38_out,
       and_39_out, and_41_out, and_45_out, and_46_out, and_49_out, and_50_out, andiins, beqins, bltins,
       bneins, comparator_1_eq, comparator_2_eq, comparator_3_eq, comparator_4_eq, comparator_5_eq,
       comparator_6_eq, comparator_7_eq, comparator_8_eq, comparator_9_eq, comparator_10_eq,
       comparator_11_eq, comparator_12_eq, comparator_13_eq, comparator_14_eq, comparator_23_eq,
       comparator_24_eq, comparator_25_eq, comparator_26_eq, comparator_27_eq, comparator_28_eq,
       comparator_29_eq, comparator_30_eq, comparator_31_eq, comparator_32_eq, comparator_33_eq,
       comparator_34_eq, comparator_35_eq, comparator_36_eq, comparator_37_eq, comparator_38_eq,
       comparator_39_eq, comparator_40_eq, comparator_41_eq, comparator_42_eq, comparator_43_eq,
       comparator_44_eq, comparator_45_eq, comparator_46_eq, comparator_47_eq, comparator_48_eq,
       comparator_49_eq, comparator_50_eq, comparator_51_eq, comparator_52_eq, comparator_53_eq,
       comparator_54_eq, div8ins, ITypejalr, ITypeleft, ITypeload, Itypetotal, jalrins, lbins, lhins, luiins,
       lwins, mul10ins, mulh11ins, not_1_out, or2ins, or_5_out, or_10_out, or_14_out, or_16_out, oriins,
       rem9ins, RType, SBType, sll6ins, slliins, slt7ins, sltiins, sra5ins, sraiins, srl4ins, srliins,
       sub12ins, swins, xor3ins, xoriins;

  Comparator #(.width(3)) comparator_1 (.a(inst[14:12]), .b(3'b101), .eq(comparator_1_eq));  // open: gt, lt
  Comparator #(.width(7)) comparator_2 (.a(inst[31:25]), .b({7{1'b0}}), .eq(comparator_2_eq));  // open: gt, lt
  Comparator #(.width(3)) comparator_3 (.a(inst[14:12]), .b(3'b101), .eq(comparator_3_eq));  // open: gt, lt
  Comparator #(.width(7)) comparator_4 (.a(inst[31:25]), .b(7'b0100000), .eq(comparator_4_eq));  // open: gt, lt
  Comparator #(.width(3)) comparator_5 (.a(inst[14:12]), .b(3'b000), .eq(comparator_5_eq));  // open: gt, lt
  Comparator #(.width(3)) comparator_6 (.a(inst[14:12]), .b(3'b001), .eq(comparator_6_eq));  // open: gt, lt
  Comparator #(.width(3)) comparator_7 (.a(inst[14:12]), .b(3'b010), .eq(comparator_7_eq));  // open: gt, lt
  and and_1 (addiins, ITypeleft, comparator_8_eq);
  Comparator #(.width(3)) comparator_8 (.a(inst[14:12]), .b(3'b000), .eq(comparator_8_eq));  // open: gt, lt
  Comparator #(.width(3)) comparator_9 (.a(inst[14:12]), .b(3'b001), .eq(comparator_9_eq));  // open: gt, lt
  Comparator #(.width(7)) comparator_10 (.a(inst[31:25]), .b({7{1'b0}}), .eq(comparator_10_eq));  // open: gt, lt
  and and_2 (sltiins, ITypeleft, comparator_11_eq);
  Comparator #(.width(3)) comparator_11 (.a(inst[14:12]), .b(3'b010), .eq(comparator_11_eq));  // open: gt, lt
  Comparator #(.width(3)) comparator_12 (.a(inst[14:12]), .b(3'b100), .eq(comparator_12_eq));  // open: gt, lt
  and and_3 (and_3_out, comparator_1_eq, comparator_2_eq);
  Comparator #(.width(3)) comparator_13 (.a(inst[14:12]), .b(3'b110), .eq(comparator_13_eq));  // open: gt, lt
  Comparator #(.width(3)) comparator_14 (.a(inst[14:12]), .b(3'b111), .eq(comparator_14_eq));  // open: gt, lt
  and and_4 (and_4_out, comparator_3_eq, comparator_4_eq);
  or or_1 (ImmSel[0], MemRW, luiins);
  or or_2 (ImmSel[1], SBType, luiins);
  and and_5 (lbins, ITypeload, comparator_5_eq);
  and and_6 (lhins, ITypeload, comparator_6_eq);
  and and_7 (lwins, ITypeload, comparator_7_eq);
  and and_8 (and_8_out, comparator_9_eq, comparator_10_eq);
  and and_9 (xoriins, ITypeleft, comparator_12_eq);
  and and_10 (srliins, ITypeleft, and_3_out);
  and and_11 (oriins, ITypeleft, comparator_13_eq);
  and and_12 (andiins, ITypeleft, comparator_14_eq);
  and and_13 (sraiins, ITypeleft, and_4_out);
  and and_14 (slliins, ITypeleft, and_8_out);
  Comparator #(.width(7)) comparator_15 (.a(inst[6:0]), .b(7'b0110011), .eq(RType));  // open: gt, lt
  Comparator #(.width(7)) comparator_16 (.a(inst[6:0]), .b(7'b0000011), .eq(ITypeload));  // open: gt, lt
  Comparator #(.width(7)) comparator_17 (.a(inst[6:0]), .b(7'b0010011), .eq(ITypeleft));  // open: gt, lt
  Comparator #(.width(7)) comparator_18 (.a(inst[6:0]), .b(7'b0100011), .eq(MemRW));  // open: gt, lt
  Comparator #(.width(7)) comparator_19 (.a(inst[6:0]), .b(7'b1100011), .eq(SBType));  // open: gt, lt
  Comparator #(.width(7)) comparator_20 (.a(inst[6:0]), .b(7'b0110111), .eq(luiins));  // open: gt, lt
  Comparator #(.width(7)) comparator_21 (.a(inst[6:0]), .b(7'b1101111), .eq(ImmSel[2]));  // open: gt, lt
  Comparator #(.width(7)) comparator_22 (.a(inst[6:0]), .b(7'b1100111), .eq(ITypejalr));  // open: gt, lt
  Comparator #(.width(3)) comparator_23 (.a(inst[14:12]), .b(3'b000), .eq(comparator_23_eq));  // open: gt, lt
  Comparator #(.width(3)) comparator_24 (.a(inst[14:12]), .b(3'b010), .eq(comparator_24_eq));  // open: gt, lt
  Comparator #(.width(3)) comparator_25 (.a(inst[14:12]), .b(3'b000), .eq(comparator_25_eq));  // open: gt, lt
  Comparator #(.width(3)) comparator_26 (.a(inst[14:12]), .b(3'b100), .eq(comparator_26_eq));  // open: gt, lt
  and and_15 (jalrins, ITypejalr, comparator_23_eq);
  and and_16 (swins, MemRW, comparator_24_eq);
  and and_17 (beqins, SBType, comparator_25_eq);
  and and_18 (bltins, SBType, comparator_26_eq);
  and and_19 (BrUn, SBType, comparator_27_eq);
  Comparator #(.width(3)) comparator_27 (.a(inst[14:12]), .b(3'b110), .eq(comparator_27_eq));  // open: gt, lt
  and and_20 (bneins, SBType, comparator_28_eq);
  Comparator #(.width(3)) comparator_28 (.a(inst[14:12]), .b(3'b001), .eq(comparator_28_eq));  // open: gt, lt
  Comparator #(.width(3)) comparator_29 (.a(inst[14:12]), .b(3'b000), .eq(comparator_29_eq));  // open: gt, lt
  Comparator #(.width(7)) comparator_30 (.a(inst[31:25]), .b({7{1'b0}}), .eq(comparator_30_eq));  // open: gt, lt
  Comparator #(.width(3)) comparator_31 (.a(inst[14:12]), .b(3'b000), .eq(comparator_31_eq));  // open: gt, lt
  Comparator #(.width(7)) comparator_32 (.a(inst[31:25]), .b(7'b0000001), .eq(comparator_32_eq));  // open: gt, lt
  Comparator #(.width(3)) comparator_33 (.a(inst[14:12]), .b(3'b000), .eq(comparator_33_eq));  // open: gt, lt
  and and_21 (and_21_out, comparator_33_eq, comparator_34_eq);
  Comparator #(.width(7)) comparator_34 (.a(inst[31:25]), .b(7'b0100000), .eq(comparator_34_eq));  // open: gt, lt
  Comparator #(.width(3)) comparator_35 (.a(inst[14:12]), .b(3'b001), .eq(comparator_35_eq));  // open: gt, lt
  Comparator #(.width(7)) comparator_36 (.a(inst[31:25]), .b({7{1'b0}}), .eq(comparator_36_eq));  // open: gt, lt
  Comparator #(.width(3)) comparator_37 (.a(inst[14:12]), .b(3'b001), .eq(comparator_37_eq));  // open: gt, lt
  Comparator #(.width(7)) comparator_38 (.a(inst[31:25]), .b(7'b0000001), .eq(comparator_38_eq));  // open: gt, lt
  Comparator #(.width(3)) comparator_39 (.a(inst[14:12]), .b(3'b010), .eq(comparator_39_eq));  // open: gt, lt
  Comparator #(.width(7)) comparator_40 (.a(inst[31:25]), .b({7{1'b0}}), .eq(comparator_40_eq));  // open: gt, lt
  Comparator #(.width(3)) comparator_41 (.a(inst[14:12]), .b(3'b101), .eq(comparator_41_eq));  // open: gt, lt
  Comparator #(.width(7)) comparator_42 (.a(inst[31:25]), .b(7'b0100000), .eq(comparator_42_eq));  // open: gt, lt
  and and_22 (and_22_out, comparator_29_eq, comparator_30_eq);
  and and_23 (and_23_out, comparator_31_eq, comparator_32_eq);
  and and_24 (sub12ins, RType, and_21_out);
  and and_25 (and_25_out, comparator_35_eq, comparator_36_eq);
  and and_26 (and_26_out, comparator_37_eq, comparator_38_eq);
  and and_27 (and_27_out, comparator_39_eq, comparator_40_eq);
  and and_28 (and_28_out, comparator_41_eq, comparator_42_eq);
  or or_3 (WBSel[0], RType, luiins, ITypeleft);
  or or_4 (WBSel[1], ImmSel[2], ITypejalr);
  and and_29 (add0ins, RType, and_22_out);
  and and_30 (mul10ins, RType, and_23_out);
  and and_31 (sll6ins, RType, and_25_out);
  and and_32 (mulh11ins, RType, and_26_out);
  and and_33 (slt7ins, RType, and_27_out);
  and and_34 (sra5ins, RType, and_28_out);
  or or_5 (or_5_out, srl4ins, srl4ins, sra5ins, sll6ins, slliins, slt7ins, sub12ins, luiins, sltiins);
  or or_6 (ALUSel[3], div8ins, rem9ins, mul10ins, mulh11ins, sub12ins, luiins);
  or or_7 (ALUSel[2], srliins, sraiins, or_5_out);
  Comparator #(.width(3)) comparator_43 (.a(inst[14:12]), .b(3'b111), .eq(comparator_43_eq));  // open: gt, lt
  Comparator #(.width(7)) comparator_44 (.a(inst[31:25]), .b(7'b0000001), .eq(comparator_44_eq));  // open: gt, lt
  Comparator #(.width(3)) comparator_45 (.a(inst[14:12]), .b(3'b100), .eq(comparator_45_eq));  // open: gt, lt
  Comparator #(.width(7)) comparator_46 (.a(inst[31:25]), .b({7{1'b0}}), .eq(comparator_46_eq));  // open: gt, lt
  Comparator #(.width(3)) comparator_47 (.a(inst[14:12]), .b(3'b101), .eq(comparator_47_eq));  // open: gt, lt
  and and_35 (and_35_out, comparator_47_eq, comparator_48_eq);
  Comparator #(.width(7)) comparator_48 (.a(inst[31:25]), .b(7'b0000001), .eq(comparator_48_eq));  // open: gt, lt
  Comparator #(.width(3)) comparator_49 (.a(inst[14:12]), .b(3'b101), .eq(comparator_49_eq));  // open: gt, lt
  Comparator #(.width(7)) comparator_50 (.a(inst[31:25]), .b({7{1'b0}}), .eq(comparator_50_eq));  // open: gt, lt
  Comparator #(.width(3)) comparator_51 (.a(inst[14:12]), .b(3'b110), .eq(comparator_51_eq));  // open: gt, lt
  and and_36 (and_36_out, comparator_51_eq, comparator_52_eq);
  Comparator #(.width(7)) comparator_52 (.a(inst[31:25]), .b({7{1'b0}}), .eq(comparator_52_eq));  // open: gt, lt
  and and_37 (and_37_out, comparator_43_eq, comparator_44_eq);
  Comparator #(.width(3)) comparator_53 (.a(inst[14:12]), .b(3'b111), .eq(comparator_53_eq));  // open: gt, lt
  and and_38 (and_38_out, comparator_53_eq, comparator_54_eq);
  Comparator #(.width(7)) comparator_54 (.a(inst[31:25]), .b({7{1'b0}}), .eq(comparator_54_eq));  // open: gt, lt
  and and_39 (and_39_out, comparator_45_eq, comparator_46_eq);
  and and_40 (div8ins, RType, and_35_out);
  and and_41 (and_41_out, comparator_49_eq, comparator_50_eq);
  and and_42 (or2ins, RType, and_36_out);
  and and_43 (rem9ins, RType, and_37_out);
  and and_44 (and1ins, RType, and_38_out);
  or or_8 (ASel, SBType, ImmSel[2], 1'b0);
  not not_1 (not_1_out, BrEq);
  and and_45 (and_45_out, bltins, BrLt);
  and and_46 (and_46_out, BrUn, BrLt);
  and and_47 (xor3ins, RType, and_39_out);
  and and_48 (srl4ins, RType, and_41_out);
  or or_9 (RegWEn, Itypetotal, RType, luiins, ImmSel[2]);
  and and_49 (and_49_out, beqins, BrEq);
  or or_10 (or_10_out, ImmSel[2], jalrins);
  and and_50 (and_50_out, bneins, not_1_out);
  or or_11 (BSel, MemRW, SBType, Itypetotal, luiins, ImmSel[2], 1'b0);
  or or_12 (Itypetotal, ITypeload, ITypeleft, ITypejalr, 1'b0);
  or or_13 (PCSel, and_49_out, or_10_out, and_50_out, and_45_out, and_46_out);
  or or_14 (or_14_out, and1ins, xor3ins, xoriins, rem9ins, mulh11ins, luiins, sra5ins, sltiins, slt7ins);
  or or_15 (ALUSel[0], or_14_out, sraiins, andiins);
  or or_16 (or_16_out, xoriins, or2ins, xor3ins, slliins, slt7ins, sll6ins, mul10ins, mulh11ins, sltiins);
  or or_17 (ALUSel[1], or_16_out, oriins);

  // Other names for the same wires on the sheet: ALUselbit0 = ALUSel[0]; ALUselbit1 = ALUSel[1];
  //   ALUselbit2 = ALUSel[2]; ALUselbit3 = ALUSel[3]; bltuins = BrUn; immselbit0 = ImmSel[0]; immselbit1 = ImmSel[1];
  //   immselbit2 = ImmSel[2]; jalins = ImmSel[2]; UJType = ImmSel[2]; opcode[6:0] = inst[6:0]; rd[4:0] = inst[11:7];
  //   funct3[2:0] = inst[14:12]; rs1[4:0] = inst[19:15]; rs2[4:0] = inst[24:20]; funct7[6:0] = inst[31:25];
  //   UType = luiins; SType = MemRW

  // Notes on the sheet:
  //   INPUTS to your circuit
  //   DON'T CHANGE THE LOCATIONS OF THE INPUTS AND OUTPUTS!
  //   OUTPUT from your circuit
endmodule
