// Logisim project cpu.circ as structural Verilog: 1 circuit, main circuit main
module main (
  input  [31:0] INSTRUCTION,
  input  CLOCK,
  output [31:0] PROGRAM_COUNTER,
  output [31:0] ra,
  output [31:0] sp,
  output [31:0] t0,
  output [31:0] t1,
  output [31:0] t2,
  output [31:0] s0,
  output [31:0] s1,
  output [31:0] a0
);

  wire Aselline, branch_comp_1_breq, branch_comp_1_brlt, control_logic_1_brun, control_logic_1_bsel,
       control_logic_1_memrw, control_logic_1_regwen, PCselout;
  wire [1:0] control_logic_1_wbsel;
  wire [2:0] control_logic_1_immsel;
  wire [3:0] control_logic_1_alusel;
  wire [31:0] ALUoutput, DMEM_p5, immout, multiplexer_1_out, multiplexer_2_out, multiplexer_3_out,
       multiplexer_4_out, pc2, pc2plus4, pcplus4, pipins, rs1out, rs2out, wbresult;

  // Probe on ALUoutput
  control_logic control_logic_1 (
    .BSel(control_logic_1_bsel), .RegWEn(control_logic_1_regwen), .ASel(Aselline),
    .ImmSel(control_logic_1_immsel), .BrUn(control_logic_1_brun), .PCSel(PCselout),
    .BrLt(branch_comp_1_brlt), .BrEq(branch_comp_1_breq), .inst(pipins), .ALUSel(control_logic_1_alusel),
    .MemRW(control_logic_1_memrw), .WBSel(control_logic_1_wbsel));
  Adder #(.width(32)) adder_1 (.a(PROGRAM_COUNTER), .b(32'h4), .out(pcplus4));  // open: cin, cout
  // Probe on pcplus4
  Multiplexer #(.width(32), .enable("false")) multiplexer_1 (
    .in0(pcplus4), .in1(ALUoutput), .out(multiplexer_1_out), .sel(PCselout));
  // Probe on PCselout
  Register #(.width(32)) PC (.D(multiplexer_1_out), .clk(CLOCK), .Q(PROGRAM_COUNTER));  // open: en, clr
  // Probe on multiplexer_1_out
  Multiplexer #(.width(32), .enable("false")) multiplexer_2 (
    .in0(INSTRUCTION), .in1(32'h13), .out(multiplexer_2_out), .sel(PCselout));
  // Probe on PROGRAM_COUNTER
  imm_gen imm_gen_1 (.ImmSel(control_logic_1_immsel), .imm(immout), .inst(pipins));
  Register #(.width(32)) register_1 (.D(multiplexer_2_out), .clk(CLOCK), .Q(pipins));  // open: en, clr
  branch_comp branch_comp_1 (
    .BrEq(branch_comp_1_breq), .rs1(rs1out), .rs2(rs2out), .BrLt(branch_comp_1_brlt),
    .BrUn(control_logic_1_brun));
  Register #(.width(32)) register_2 (.D(PROGRAM_COUNTER), .clk(CLOCK), .Q(pc2));  // open: en, clr
  // Probe on pc2
  regfile_main RegFile (
    .rs2(pipins[24:20]), .rd(pipins[11:7]), .Read_Data_1(rs1out), .Read_Data_2(rs2out), .ra(ra), .sp(sp),
    .t0(t0), .t1(t1), .t2(t2), .s0(s0), .s1(s1), .a0(a0), .rs1(pipins[19:15]), .Write_Data(wbresult),
    .RegWEn(control_logic_1_regwen), .clk(CLOCK));
  Multiplexer #(.width(32), .enable("false")) multiplexer_3 (
    .in0(rs2out), .in1(immout), .out(multiplexer_3_out), .sel(control_logic_1_bsel));
  Adder #(.width(32)) adder_2 (.a(pc2), .b(32'h4), .out(pc2plus4));  // open: cin, cout
  Multiplexer #(.width(32), .enable("false")) multiplexer_4 (
    .in0(rs1out), .in1(pc2), .out(multiplexer_4_out), .sel(Aselline));
  alu Arithmetic_Logic_Unit (
    .ALUSel(control_logic_1_alusel), .Result(ALUoutput), .A(multiplexer_4_out), .B(multiplexer_3_out));
  // mem_main DMEM: pin names not known; wires that end beside it: ALUoutput, rs2out, CLOCK, control_logic_1_memrw, DMEM_p5
  Multiplexer #(.select(2), .width(32), .enable("false")) multiplexer_5 (
    .in0(DMEM_p5), .in1(ALUoutput), .in2(pc2plus4), .out(wbresult), .sel(control_logic_1_wbsel));  // open: in3

  // Other names for the same wires on the sheet: clk = CLOCK; rd[4:0] = pipins[11:7]; rs1[4:0] = pipins[19:15];
  //   rs2[4:0] = pipins[24:20]

  // Notes on the sheet:
  //   Output
  //   IMEM (do **NOT** move this)
  //   Inputs
  //   It is OK to move the PC, RegFile, ALU, MEM, Branch Comp, Imm Gen, and Control Logic to wherever is most convenient for you when constructing your CPU, and to delete this text
  //   Inputs/Outputs for testing. Do **NOT** move these.
endmodule
