// Logisim project imm_gen.circ as structural Verilog: 1 circuit, main circuit imm_gen
module imm_gen (
  input  [31:0] inst,
  input  [2:0] ImmSel,
  output [31:0] imm
);

  wire [31:0] IType, SBType, SType, UJType;

  Multiplexer #(.select(3), .width(32), .enable("false")) multiplexer_1 (
    .in0(IType), .in1(SType), .in2(SBType), .in3({inst[31:12], {12{1'b0}}}), .in4(UJType), .out(imm),
    .sel(ImmSel));  // open: in5, in6, in7
  assign IType = {{20{inst[31]}}, inst[31:20]};  // Bit_Extender bit_extender_1
  assign SType = {{20{inst[31]}}, {inst[31:25], inst[11:7]}};  // Bit_Extender bit_extender_2
  assign SBType = {{19{inst[31]}}, {inst[31], inst[7], inst[30:25], inst[11:8], 1'b0}};  // Bit_Extender bit_extender_3
  assign UJType = {{11{inst[31]}}, {inst[31], inst[19:12], inst[20], inst[30:21], 1'b0}};  // Bit_Extender bit_extender_4

  // Other names for the same wires on the sheet: UType[31:12] = inst[31:12]

  // Notes on the sheet:
  //   INPUTS to your circuit
  //   DON'T CHANGE THE LOCATIONS OF THE INPUTS AND OUTPUTS!
  //   OUTPUT from your circuit
endmodule
