// Logisim project regfile.circ as structural Verilog: 1 circuit, main circuit main
module main (
  input  [4:0] rs1,
  input  [4:0] rs2,
  input  [4:0] rd,
  input  [31:0] Write_Data,
  input  RegWEn,
  input  clk,
  output [31:0] ra,
  output [31:0] sp,
  output [31:0] t0,
  output [31:0] t1,
  output [31:0] t2,
  output [31:0] s0,
  output [31:0] s1,
  output [31:0] a0,
  output [31:0] Read_Data_1,
  output [31:0] Read_Data_2
);

  wire a0en, raen, s0en, s1en, spen, t0en, t1en, t2en;
  wire [31:0] a0temp, ratemp, s0temp, s1temp, sptemp, t0temp, t1temp, t2temp;

  Register #(.width(32)) register_1 (.D(sptemp), .en(spen), .clk(clk), .Q(sp));  // open: clr
  Register #(.width(32)) register_2 (.D(t0temp), .en(t0en), .clk(clk), .Q(t0));  // open: clr
  Register #(.width(32)) register_3 (.D(t1temp), .en(t1en), .clk(clk), .Q(t1));  // open: clr
  Register #(.width(32)) register_4 (.D(s0temp), .en(s0en), .clk(clk), .Q(s0));  // open: clr
  Register #(.width(32)) register_5 (.D(t2temp), .en(t2en), .clk(clk), .Q(t2));  // open: clr
  Register #(.width(32)) register_6 (.D(ratemp), .en(raen), .clk(clk), .Q(ra));  // open: clr
  Demultiplexer #(.select(5), .width(32), .enable("false")) demultiplexer_1 (
    .out1(ratemp), .out2(sptemp), .out5(t0temp), .out6(t1temp), .out7(t2temp), .out8(s0temp), .out9(s1temp),
    .out10(a0temp), .in(Write_Data), .sel(rd));  // open: out0, out3, out4, out11, out12, out13, out14, out15, out16, out17, out18, out19, out20, out21, out22, out23, out24, out25, out26, out27, out28, out29, out30, out31
  Register #(.width(32)) register_7 (.D(s1temp), .en(s1en), .clk(clk), .Q(s1));  // open: clr
  Register #(.width(32)) register_8 (.D(a0temp), .en(a0en), .clk(clk), .Q(a0));  // open: clr
  Multiplexer #(.select(5), .width(32), .enable("false")) multiplexer_1 (
    .in0({32{1'b0}}), .in1(ra), .in2(sp), .in5(t0), .in6(t1), .in7(t2), .in8(s0), .in9(s1), .in10(a0),
    .out(Read_Data_1), .sel(rs1));  // open: in3, in4, in11, in12, in13, in14, in15, in16, in17, in18, in19, in20, in21, in22, in23, in24, in25, in26, in27, in28, in29, in30, in31
  Multiplexer #(.select(5), .width(32), .enable("false")) multiplexer_2 (
    .in0({32{1'b0}}), .in1(ra), .in2(sp), .in5(t0), .in6(t1), .in7(t2), .in8(s0), .in9(s1), .in10(a0),
    .out(Read_Data_2), .sel(rs2));  // open: in3, in4, in11, in12, in13, in14, in15, in16, in17, in18, in19, in20, in21, in22, in23, in24, in25, in26, in27, in28, in29, in30, in31
  Demultiplexer #(.select(5), .enable("false")) demultiplexer_2 (
    .out1(raen), .out2(spen), .out5(t0en), .out6(t1en), .out7(t2en), .out8(s0en), .out9(s1en), .out10(a0en),
    .in(RegWEn), .sel(rd));  // open: out0, out3, out4, out11, out12, out13, out14, out15, out16, out17, out18, out19, out20, out21, out22, out23, out24, out25, out26, out27, out28, out29, out30, out31

  // Other names for the same wires on the sheet: read_data1[31:0] = Read_Data_1; read_data2[31:0] = Read_Data_2;
  //   read_reg1[4:0] = rs1; read_reg2[4:0] = rs2; write_en = RegWEn; write_reg[4:0] = rd

  // Notes on the sheet:
  //   INPUTS to your circuit
  //   DON'T CHANGE THE LOCATIONS OF THE INPUTS AND OUTPUTS!
  //   These are DEBUG/TEST outputs from your circuit.
  //   OUTPUTS from your circuit
endmodule
